# Fritzing sketch SolderFan (saved by Fritzing 0.9.3b)
circuit board: 8.46667cm x 5.64444cm
breadboards: 1

parts:
  S2 = Pushbutton [package="[THT]"]
  M1 = DC Motor
  VCC1 = Battery

nets:
  N1: S2.Pin_1, S2.Pin_2, VCC1.+
  N2: S2.Pin_3, S2.Pin_4, M1.pin_1
  N3: M1.pin_2, VCC1.-

notes:
  Fan
  Switch
